// Logisim project CRCs-code.circ as structural Verilog: 2 circuits, main circuit CRC
module CRC (
  input  [7:0] data,
  input  [3:0] \除数 ,
  output [10:0] \output 
);

  wire \division_1_商 , \division_2_商 , \division_3_商 , \division_6_商 ;
  wire [2:0] data_t, \division_1__3位余数 , \division_2__3位余数 , \division_3__3位余数 , \division_4__3位余数 ,
       \division_5__3位余数 , \division_6__3位余数 , \division_7__3位余数 ;
  wire [10:0] bit_extender_1_out;

  assign bit_extender_1_out = {{3{1'b0}}, data};  // Bit_Extender bit_extender_1
  Shifter #(.width(11)) shifter_1 (.in(bit_extender_1_out), .\dist (4'b0011), .out({\output [10:3], data_t}));
  division division_1 (.\被除数 (\output [10:7]), .\除数 (\除数 ), .\_3位余数 (\division_1__3位余数 ), .\商 (\division_1_商 ));
  division division_2 (
    .\被除数 ({\division_1__3位余数 , \output [6]}), .\除数 (\除数 ), .\_3位余数 (\division_2__3位余数 ), .\商 (\division_2_商 ));
  division division_3 (
    .\被除数 ({\division_2__3位余数 , \output [5]}), .\除数 (\除数 ), .\_3位余数 (\division_3__3位余数 ), .\商 (\division_3_商 ));
  division division_4 (
    .\被除数 ({\division_3__3位余数 , \output [4]}), .\除数 (\除数 ), .\_3位余数 (\division_4__3位余数 ));  // open: 商
  division division_5 (
    .\被除数 ({\division_4__3位余数 , \output [3]}), .\除数 (\除数 ), .\_3位余数 (\division_5__3位余数 ));  // open: 商
  division division_6 (
    .\被除数 ({\division_5__3位余数 , data_t[2]}), .\除数 (\除数 ), .\_3位余数 (\division_6__3位余数 ), .\商 (\division_6_商 ));
  division division_7 (.\被除数 ({\division_6__3位余数 , data_t[1]}), .\除数 (\除数 ), .\_3位余数 (\division_7__3位余数 ));  // open: 商
  // Probe on \output [2:0]
  division division_8 (.\被除数 ({\division_7__3位余数 , data_t[0]}), .\除数 (\除数 ), .\_3位余数 (\output [2:0]));  // open: 商

  // Other names for the same wires on the sheet: data_t[10:3] = \output [10:3]
endmodule

module division (
  input  [3:0] \被除数 ,
  input  [3:0] \除数 ,
  output [2:0] \_3位余数 ,
  output \商 
);

  wire [3:0] xor_1_out;
  wire [3:3] multiplexer_1_out;

  BitSelector #(.width(4)) bitselector_1 (.in(\被除数 ), .out(\商 ), .sel(2'b11));
  assign xor_1_out = \被除数  ^ \除数 ;  // XOR_Gate xor_1, 4 bits wide
  Multiplexer #(.width(4)) multiplexer_1 (
    .in0(\被除数 ), .in1(xor_1_out), .out({multiplexer_1_out[3], \_3位余数 }), .sel(\商 ));  // open: en

  // Other names for the same wires on the sheet: num[3:0] = \被除数 ; quotient = \商 

  // Notes on the sheet:
  //   首位必为1
  //   四位模二除法器
  //   等价于异或运算
endmodule
