// Logisim project FSM.circ as structural Verilog: 2 circuits, main circuit fsm
module fsm (
  input  CLR,
  input  [1:0] In,
  output out
);

  wire clock_1_out, not_1_out;
  wire [2:0] current, multiplexer_1_out, next_state_1_o0;

  next_state next_state_1 (
    .In2(current[2]), .In1(current[1]), .In0(current[0]), .char1(In[1]), .char0(In[0]),
    .O2(next_state_1_o0[2]), .O1(next_state_1_o0[1]), .O0(next_state_1_o0[0]));
  // Probe on next_state_1_o0
  Multiplexer #(.width(3)) multiplexer_1 (
    .in0(next_state_1_o0), .in1(3'b000), .out(multiplexer_1_out), .sel(CLR));  // open: en
  Clock clock_1 (.out(clock_1_out));
  Register #(.width(3)) register_1 (.D(multiplexer_1_out), .Q(current), .clk(clock_1_out));  // open: en, clr
  not not_1 (not_1_out, In[0]);
  and and_1 (out, current[0], current[1], not_1_out);

  // Notes on the sheet:
  //   同步复位标准做法
endmodule

module next_state (
  input  In2,
  input  In1,
  input  In0,
  input  char1,
  input  char0,
  output O2,
  output O1,
  output O0
);

  wire and_2_out, and_3_out, and_4_out, and_5_out, and_6_out, and_7_out, and_8_out, not_1_out, not_2_out,
       not_3_out, not_4_out, not_5_out, not_6_out, not_7_out, not_8_out, not_9_out, not_10_out, not_11_out,
       not_12_out, not_13_out, not_14_out;

  not not_1 (not_1_out, char0);
  not not_2 (not_2_out, In1);
  not not_3 (not_3_out, char1);
  not not_4 (not_4_out, In1);
  not not_5 (not_5_out, char0);
  not not_6 (not_6_out, In0);
  not not_7 (not_7_out, char0);
  not not_8 (not_8_out, In0);
  not not_9 (not_9_out, char1);
  not not_10 (not_10_out, In1);
  not not_11 (not_11_out, char0);
  not not_12 (not_12_out, In0);
  not not_13 (not_13_out, char0);
  not not_14 (not_14_out, char1);
  and and_1 (O2, In1, In0, not_1_out);
  and and_2 (and_2_out, not_2_out, In0, not_3_out);
  and and_3 (and_3_out, not_4_out, In0, not_5_out);
  and and_4 (and_4_out, In1, not_6_out, not_7_out);
  and and_5 (and_5_out, not_8_out, not_9_out, char0);
  and and_6 (and_6_out, not_10_out, In0, not_11_out);
  and and_7 (and_7_out, In1, not_12_out, not_13_out);
  and and_8 (and_8_out, In1, not_14_out, char0);
  or or_1 (O1, and_2_out, and_3_out, and_4_out);
  or or_2 (O0, and_5_out, and_6_out, and_7_out, and_8_out);
endmodule
