// Logisim project FSM2.circ as structural Verilog: 2 circuits, main circuit fsm
module fsm (
  input  CLR,
  input  [1:0] In,
  output out
);

  wire clock_1_out, not_1_out;
  wire [2:0] current, multiplexer_1_out, next_state_1_o0;

  next_state next_state_1 (
    .State2(current[2]), .State1(current[1]), .State0(current[0]), .In1(In[1]), .In0(In[0]),
    .O2(next_state_1_o0[2]), .O1(next_state_1_o0[1]), .O0(next_state_1_o0[0]));
  // Probe on next_state_1_o0
  Multiplexer #(.width(3)) multiplexer_1 (
    .in0(next_state_1_o0), .in1(3'b000), .out(multiplexer_1_out), .sel(CLR));  // open: en
  Clock clock_1 (.out(clock_1_out));
  // Probe on current
  Register #(.width(3)) register_1 (.D(multiplexer_1_out), .Q(current), .clk(clock_1_out));  // open: en, clr
  not not_1 (not_1_out, In[0]);
  and and_1 (out, current[2], not_1_out);

  // Notes on the sheet:
  //   同步复位标准做法
endmodule

module next_state (
  input  State2,
  input  State1,
  input  State0,
  input  In1,
  input  In0,
  output O2,
  output O1,
  output O0
);

  wire and_1_out, and_2_out, and_3_out, and_4_out, and_5_out, not_1_out, not_2_out, not_3_out, not_4_out,
       not_5_out, not_6_out, not_7_out, not_8_out, not_9_out, not_10_out, not_11_out, not_12_out, not_13_out,
       not_14_out, not_15_out, not_16_out, not_17_out, not_18_out, not_19_out;

  not not_1 (not_1_out, State2);
  not not_2 (not_2_out, State1);
  not not_3 (not_3_out, In0);
  not not_4 (not_4_out, State2);
  not not_5 (not_5_out, State0);
  not not_6 (not_6_out, In0);
  not not_7 (not_7_out, State2);
  not not_8 (not_8_out, State1);
  not not_9 (not_9_out, In1);
  not not_10 (not_10_out, State2);
  not not_11 (not_11_out, State0);
  not not_12 (not_12_out, In1);
  not not_13 (not_13_out, State1);
  not not_14 (not_14_out, State0);
  not not_15 (not_15_out, In1);
  not not_16 (not_16_out, State2);
  not not_17 (not_17_out, State1);
  not not_18 (not_18_out, State0);
  not not_19 (not_19_out, In1);
  and and_1 (and_1_out, not_1_out, not_2_out, State0, not_3_out);
  and and_2 (and_2_out, not_4_out, State1, not_5_out, not_6_out);
  and and_3 (and_3_out, not_7_out, not_8_out, State0, not_9_out, In0);
  and and_4 (and_4_out, not_10_out, State1, not_11_out, not_12_out, In0);
  and and_5 (and_5_out, State2, not_13_out, not_14_out, not_15_out, In0);
  and and_6 (O0, not_16_out, not_17_out, not_18_out, not_19_out, In0);
  or or_1 (O2, and_1_out, and_2_out);
  or or_2 (O1, and_3_out, and_4_out, and_5_out);
endmodule
