// Logisim project P0_ups_and_downs .circ as structural Verilog: 2 circuits, main circuit main
module main (
  input  clk,
  input  reset,
  input  [4:0] a,
  output out_4
);

  wire cnt, comparator_1_gt, comparator_2_eq, counter_2_q;
  wire [2:0] register_2_q, state_transfer_1_o0;
  wire [4:0] an_1, register_1_q;

  Counter #(.width(1), .max('h1), .ongoal("stay")) counter_1 (
    .Q(cnt), .clk(clk), .clr(reset));  // open: load, D, count, carry
  Comparator #(.width(5)) comparator_1 (.a(a), .b(an_1), .gt(comparator_1_gt));  // open: eq, lt
  state_transfer state_transfer_1 (
    .S2(register_2_q[2]), .S1(register_2_q[1]), .S0(register_2_q[0]), .Y1(comparator_1_gt),
    .o2(state_transfer_1_o0[2]), .o1(state_transfer_1_o0[1]), .o0(state_transfer_1_o0[0]));
  Register #(.width(5)) register_1 (.D(a), .Q(register_1_q), .clk(clk));  // open: en, clr
  Multiplexer #(.width(5)) multiplexer_1 (.in0(5'b00111), .in1(register_1_q), .out(an_1), .sel(cnt));  // open: en
  // Probe on an_1
  Register #(.width(3)) register_2 (.D(state_transfer_1_o0), .Q(register_2_q), .clk(clk), .clr(reset));  // open: en
  Comparator #(.width(3)) comparator_2 (.a(register_2_q), .b(3'b100), .eq(comparator_2_eq));  // open: gt, lt
  Counter #(.width(1), .max('h1), .ongoal("stay")) counter_2 (
    .Q(counter_2_q), .clk(clk), .clr(reset));  // open: load, D, count, carry
  Multiplexer multiplexer_2 (.in0(1'b0), .in1(comparator_2_eq), .out(out_4), .sel(counter_2_q));  // open: en

  // Other names for the same wires on the sheet: an[4:0] = a

  // Notes on the sheet:
  //   初始化
  //   存储an-1
endmodule

module state_transfer (
  input  S2,
  input  S1,
  input  S0,
  input  Y1,
  output o2,
  output o1,
  output o0
);

  wire and_1_out, and_2_out, and_3_out, and_4_out, and_5_out, and_6_out, and_7_out, and_8_out, and_9_out,
       not_1_out, not_2_out, not_3_out, not_4_out, not_5_out, not_6_out, not_7_out;

  and and_1 (and_1_out, S1, S0, Y1);
  and and_2 (and_2_out, S2, S1);
  not not_1 (not_1_out, S1);
  and and_3 (and_3_out, not_1_out, S0, Y1);
  and and_4 (and_4_out, S1, not_2_out);
  not not_2 (not_2_out, S0);
  and and_5 (and_5_out, S2, Y1);
  and and_6 (and_6_out, S2, S0);
  not not_3 (not_3_out, S2);
  not not_4 (not_4_out, S1);
  not not_5 (not_5_out, S0);
  not not_6 (not_6_out, S0);
  not not_7 (not_7_out, Y1);
  or or_1 (o2, and_1_out, and_2_out);
  or or_2 (o1, and_3_out, and_4_out, and_5_out, and_6_out);
  and and_7 (and_7_out, not_3_out, not_4_out, not_5_out, Y1);
  and and_8 (and_8_out, S1, not_6_out, not_7_out);
  or or_3 (o0, and_7_out, and_8_out, and_9_out);
  and and_9 (and_9_out, S2, S0);
endmodule
