// Logisim project navigation.circ as structural Verilog: 4 circuits, main circuit navigation
module navigation (
  input  [1:0] dir,
  input  clk,
  input  reset,
  input  [1:0] Input,
  output arrive,
  output hit,
  output \output ,
  output [1:0] flag
);

  wire comparator_1_eq;
  wire [1:0] others, register_1_q, \同步复位在此插入MUX ;
  wire [2:0] current_state, state_transfer_1_next0;

  // Probe on current_state
  next_state next_state_1 (.in_1(Input), .in_2(\同步复位在此插入MUX ), .out_3(\同步复位在此插入MUX ));
  state_transfer state_transfer_1 (
    .dir1(dir[1]), .dir0(dir[0]), .state2(current_state[2]), .state1(current_state[1]),
    .state0(current_state[0]), .next2(state_transfer_1_next0[2]), .next1(state_transfer_1_next0[1]),
    .next0(state_transfer_1_next0[0]));
  // Probe on state_transfer_1_next0[0]
  next_state next_state_2 (.in_1(\同步复位在此插入MUX ), .in_2(others), .out_3(flag));
  Register #(.width(2)) register_1 (.D(\同步复位在此插入MUX ), .Q(register_1_q), .clk(clk), .clr(reset));  // open: en
  // Probe on current_state
  Register #(.width(3)) register_2 (.D(state_transfer_1_next0), .Q(current_state), .clk(clk), .clr(reset));  // open: en
  Comparator #(.width(3)) comparator_1 (
    .a(state_transfer_1_next0), .b(current_state), .eq(comparator_1_eq));  // open: gt, lt
  state_out state_out_1 (.in_1(register_1_q), .out_2(\output ));
  Register #(.width(1)) register_3 (.D(comparator_1_eq), .Q(hit), .clk(clk), .clr(reset));  // open: en
  Comparator #(.width(3)) comparator_2 (.a(current_state), .b(3'b100), .eq(arrive));  // open: gt, lt

  // Other names for the same wires on the sheet: 异步复位在此插入MUX = \output 

  // Notes on the sheet:
  //   状态少，可以使用真值表法直接列出来
  //   state-transfer
  //   过程中的特殊判断
  //   state-out
endmodule

module state_transfer (
  input  dir0,
  input  dir1,
  input  state0,
  input  state1,
  input  state2,
  output next2,
  output next1,
  output next0
);

  wire and_1_out, and_2_out, and_3_out, and_4_out, and_5_out, and_6_out, and_7_out, and_8_out, and_9_out,
       and_10_out, and_11_out, not_1_out, not_2_out, not_3_out, not_4_out, not_5_out, not_6_out, not_7_out,
       not_8_out, not_9_out, not_10_out, not_11_out, not_12_out, not_13_out, not_14_out, not_15_out,
       not_16_out, not_17_out, not_18_out, not_19_out, not_20_out, not_21_out, not_22_out, not_23_out,
       not_24_out, not_25_out, not_26_out, not_27_out;

  not not_1 (not_1_out, dir1);
  not not_2 (not_2_out, dir0);
  not not_3 (not_3_out, state2);
  not not_4 (not_4_out, state0);
  not not_5 (not_5_out, dir1);
  not not_6 (not_6_out, state2);
  not not_7 (not_7_out, dir1);
  not not_8 (not_8_out, dir0);
  not not_9 (not_9_out, state2);
  not not_10 (not_10_out, dir1);
  not not_11 (not_11_out, state2);
  not not_12 (not_12_out, state1);
  not not_13 (not_13_out, dir1);
  not not_14 (not_14_out, state2);
  not not_15 (not_15_out, state0);
  not not_16 (not_16_out, dir0);
  not not_17 (not_17_out, state2);
  not not_18 (not_18_out, state0);
  not not_19 (not_19_out, state2);
  not not_20 (not_20_out, dir1);
  not not_21 (not_21_out, dir0);
  not not_22 (not_22_out, state2);
  not not_23 (not_23_out, state1);
  not not_24 (not_24_out, dir0);
  not not_25 (not_25_out, state2);
  not not_26 (not_26_out, state2);
  not not_27 (not_27_out, state2);
  and and_1 (and_1_out, not_1_out, not_2_out, not_3_out, state1, not_4_out);
  and and_2 (and_2_out, not_5_out, dir0, not_6_out, state1, state0);
  and and_3 (and_3_out, not_7_out, not_8_out, not_9_out, state0);
  and and_4 (and_4_out, not_10_out, not_11_out, not_12_out, state0);
  and and_5 (and_5_out, not_13_out, dir0, not_14_out, state1, not_15_out);
  and and_6 (and_6_out, dir1, not_16_out, not_17_out, state1, not_18_out);
  and and_7 (and_7_out, dir1, dir0, not_19_out, state1, state0);
  and and_8 (and_8_out, not_20_out, not_21_out, not_22_out, not_23_out);
  and and_9 (and_9_out, not_24_out, not_25_out, state1, state0);
  and and_10 (and_10_out, dir1, dir0, not_26_out, state0);
  and and_11 (and_11_out, dir1, dir0, not_27_out, state1);
  or or_1 (next2, and_1_out, and_2_out);
  or or_2 (next1, and_3_out, and_4_out, and_5_out, and_6_out, and_7_out);
  or or_3 (next0, and_8_out, and_9_out, and_10_out, and_11_out);
endmodule

module next_state (
  input  [1:0] in_1,
  input  [1:0] in_2,
  output [1:0] out_3
);
endmodule

module state_out (
  input  [1:0] in_1,
  output out_2
);
endmodule
