// Logisim project single_process_CPU.circ as structural Verilog: 10 circuits, main circuit main
module main (
  input  in_1,
  output [31:0] out_2,
  output [31:0] out_3,
  output out_4,
  output [4:0] out_5,
  output [31:0] out_6,
  output out_7,
  output [31:0] out_8,
  output [31:0] out_9
);

  wire ALUSrc, clk, controller_1_memtoreg, ExtOp, MemtoReg, RegDst, zero;
  wire [1:0] nPC_Sel;
  wire [2:0] ALU_Ctrl;
  wire [5:0] undriven;
  wire [31:0] dm_1_rd, grf_1_rd1, imm16_EXT, multiplexer_3_out, npc_1_npc, pc_1_do;

  Clock clock_1 (.out(clk));
  Clock clock_2 (.out(clk));
  PC pc_1 (.DI(npc_1_npc), .reset(in_1), .clk(clk), .DO(pc_1_do));
  NPC npc_1 (.PC(pc_1_do), .imm(out_2[15:0]), .NPC(npc_1_npc), .nPC_Sel(nPC_Sel), .zero(zero));
  IM im_1 (.PC(pc_1_do), .Program(out_2));
  Controller controller_1 (
    .op(out_2[31:26]), .funct(undriven), .RegDst(RegDst), .ALUSrc(ALUSrc), .MemtoReg(controller_1_memtoreg),
    .RegWrite(out_4), .MemWrite(out_7), .nPC_Sel(nPC_Sel), .ExtOp(ExtOp), .ALU_op(ALU_Ctrl));
  EXT ext_1 (.Input(out_2[15:0]), .Out(imm16_EXT), .EXT_op_2(ExtOp));
  Multiplexer #(.width(5)) multiplexer_1 (
    .in0(out_2[25:21]), .in1(out_2[15:11]), .out(out_5), .sel(RegDst));  // open: en
  Multiplexer #(.width(32)) multiplexer_2 (.in0(out_8), .in1(dm_1_rd), .out(out_6), .sel(MemtoReg));  // open: en
  GRF grf_1 (
    .A1(out_2[25:21]), .A2(out_2[25:21]), .A3(out_5), .WD(out_6), .RD1(grf_1_rd1), .RD2(out_9), .clk(clk),
    .reset(in_1), .WE(out_4));
  Multiplexer #(.width(32)) multiplexer_3 (
    .in0(out_9), .in1(imm16_EXT), .out(multiplexer_3_out), .sel(ALUSrc));  // open: en
  ALU_2 alu_2_1 (.zero(zero), .out_6(out_8), .A(grf_1_rd1), .B_2(multiplexer_3_out), .ALUop(ALU_Ctrl));
  DM dm_1 (.addr(out_8), .WD(out_9), .WE(out_7), .clk(clk), .reset(in_1), .RD(dm_1_rd));

  // Other names for the same wires on the sheet: imm16[15:0] = out_2[15:0]; Instr[31:0] = out_2;
  //   MemAddr[31:0] = out_8; MemData[31:0] = out_9; MemWrite = out_7; PC[31:0] = out_3; RegAddr[4:0] = out_5;
  //   RegData[31:0] = out_6; RegWrite = out_4; reset = in_1

  // Notes on the sheet:
  //   opcode
  //   funct
  //   rt
  //   rd
  //   rs
  //   shamt
  //   imm16
  //   debug 2 A B swap
  //   debug 1 RD1 - WD not rst to WD
endmodule

module PC (
  input  [31:0] DI,
  input  reset,
  input  clk,
  output [31:0] DO
);

  wire counter_1_q;
  wire [31:0] register_1_q;

  Register #(.width(32)) register_1 (.D(DI), .Q(register_1_q), .clk(clk), .clr(reset));  // open: en
  Counter #(.width(1), .max('h1), .ongoal("stay")) counter_1 (
    .Q(counter_1_q), .clk(clk), .clr(reset));  // open: load, D, count, carry
  Multiplexer #(.width(32)) multiplexer_1 (
    .in0(32'h3000), .in1(register_1_q), .out(DO), .sel(counter_1_q));  // open: en

  // Notes on the sheet:
  //   debug4 clk connected to reset
endmodule

module NPC (
  input  [31:0] PC,
  input  [15:0] imm,
  input  zero,
  input  [1:0] nPC_Sel,
  output [31:0] NPC
);

  wire PC_cout, undriven_2;
  wire [31:0] bit_extender_1_out, multiplexer_1_out, PC_out, shifter_1_out, undriven, undriven_3;

  assign bit_extender_1_out = {{16{imm[15]}}, imm};  // Bit_Extender bit_extender_1
  Shifter #(.width(32)) shifter_1 (.in(bit_extender_1_out), .\dist (5'b00010), .out(shifter_1_out));
  Adder #(.width(32), .tristate("false")) u_PC (
    .a(undriven), .b(shifter_1_out), .out(PC_out), .cin(undriven_2), .cout(PC_cout));
  Adder #(.width(32)) adder_1 (.a(undriven), .b(shifter_1_out), .out(PC_out), .cin(undriven_2), .cout(PC_cout));
  Multiplexer #(.width(32)) multiplexer_1 (
    .in0(undriven), .in1(PC_out), .out(multiplexer_1_out), .sel(zero));  // open: en
  Multiplexer #(.select(2), .width(32)) multiplexer_2 (
    .in0(undriven), .in1(multiplexer_1_out), .in2(multiplexer_1_out), .in3(undriven_3), .out(NPC),
    .sel(nPC_Sel), .en(1'b1));
  Multiplexer #(.select(2), .width(32)) multiplexer_3 (
    .in0(undriven), .in1(multiplexer_1_out), .in2(multiplexer_1_out), .in3(undriven_3), .out(NPC),
    .sel(nPC_Sel), .en(1'b1));
endmodule

module IM (
  input  [31:0] PC,
  output [31:0] Program
);

  wire [11:0] bitselector_1_out;
  wire [31:0] shifter_1_out, subtractor_1_out;

  Subtractor #(.width(32)) subtractor_1 (.a(PC), .b(32'h3000), .out(subtractor_1_out));  // open: bin, bout
  Shifter #(.width(32), .shift("lr")) shifter_1 (.in(subtractor_1_out), .\dist (5'b00010), .out(shifter_1_out));
  BitSelector #(.width(32), .group(12)) bitselector_1 (.in(shifter_1_out), .out(bitselector_1_out), .sel(2'b00));
  ROM #(.addrWidth(12), .dataWidth(32)) rom_1 (.addr(bitselector_1_out), .data(Program));  // open: sel

  // Notes on the sheet:
  //   contents of rom_1 (hex, n*v repeats v):
  //   3c0f8000 35ef0000
endmodule

module GRF (
  input  clk,
  input  reset,
  input  WE,
  input  [4:0] A1,
  input  [4:0] A2,
  input  [4:0] A3,
  input  [31:0] WD,
  output [31:0] RD1,
  output [31:0] RD2
);

  wire undriven;
  wire [31:0] a_06, demultiplexer_1_out0, demultiplexer_1_out31, in_00, in_01, in_02, in_03, in_04, in_05,
       in_06, in_07, in_08, in_09, in_10, in_11, in_12, in_13, in_14, in_15, in_16, in_17, in_18, in_19,
       in_20, in_21, in_22, in_23, in_24, in_25, in_26, in_27, in_28, in_30, in_31, o_00, o_01, o_02, o_03,
       o_04, o_05, o_06, o_07, o_08, o_09, o_10, o_11, o_12, o_13, o_14, o_15, o_16, o_17, o_18, o_19, o_20,
       o_21, o_22, o_23, o_24, o_25, o_26, o_27, o_28, o_29, o_30, o_31, undriven_2;

  Register #(.width(32)) a_00 (.D(in_00), .Q(o_00), .clk(clk), .clr(reset));  // open: en
  Register #(.width(32)) a_04 (.D(in_04), .Q(o_04), .clk(clk), .clr(reset));  // open: en
  Register #(.width(32)) a_08 (.D(in_08), .Q(o_08), .clk(clk), .clr(reset));  // open: en
  Register #(.width(32)) a_12 (.D(in_12), .Q(o_12), .clk(clk), .clr(reset));  // open: en
  Register #(.width(32)) a_16 (.D(in_16), .Q(o_16), .clk(clk), .clr(reset));  // open: en
  Register #(.width(32)) a_20 (.D(in_20), .Q(o_20), .clk(clk), .clr(reset));  // open: en
  Register #(.width(32)) a_28 (.D(in_28), .Q(in_18), .clk(clk), .clr(undriven));  // open: en
  Register #(.width(32)) a_01 (.D(in_01), .Q(o_01), .clk(clk), .clr(reset));  // open: en
  Register #(.width(32)) a_05 (.D(in_05), .Q(o_05), .clk(clk), .clr(reset));  // open: en
  Register #(.width(32)) a_09 (.D(in_09), .Q(o_09), .clk(reset), .clr(reset));  // open: en
  Register #(.width(32)) a_13 (.D(in_13), .Q(o_13), .clk(reset), .clr(reset));  // open: en
  Register #(.width(32)) a_17 (.D(in_17), .Q(o_17), .clk(clk), .clr(reset));  // open: en
  Register #(.width(32)) a_21 (.D(in_21), .Q(o_21), .clk(clk), .clr(reset));  // open: en
  Register #(.width(32)) a_25 (.D(in_25), .Q(o_25), .clk(clk), .clr(clk));  // open: en
  Register #(.width(32)) a_02 (.D(in_02), .Q(o_02), .clk(clk), .clr(reset));  // open: en
  Register #(.width(32)) u_a_06 (.D(in_06), .Q(o_06), .clk(clk), .clr(reset));  // open: en
  Register #(.width(32)) a_10 (.D(in_10), .Q(o_10), .clk(clk), .clr(reset));  // open: en
  Register #(.width(32)) a_14 (.D(in_14), .Q(o_14), .clk(clk), .clr(reset));  // open: en
  Register #(.width(32)) a_18 (.D(in_18), .Q(o_18), .clk(clk), .clr(reset));  // open: en
  Register #(.width(32)) a_22 (.D(in_22), .Q(o_22), .clk(clk), .clr(reset));  // open: en
  Register #(.width(32)) a_26 (.D(in_26), .Q(o_26), .clk(clk), .clr(reset));  // open: en
  Register #(.width(32)) a_30 (.D(in_30), .Q(o_30), .clk(clk), .clr(reset));  // open: en
  Register #(.width(32)) a_03 (.D(in_03), .Q(o_03), .clk(clk), .clr(reset));  // open: en
  Register #(.width(32)) a_07 (.D(in_07), .Q(o_07), .clk(clk), .clr(reset));  // open: en
  Register #(.width(32)) a_11 (.D(in_11), .Q(in_08), .clk(clk), .clr(reset));  // open: en
  Register #(.width(32)) a_15 (.D(in_15), .Q(o_15), .clk(clk), .clr(reset));  // open: en
  Register #(.width(32)) a_19 (.D(in_19), .Q(o_19), .clk(clk), .clr(reset));  // open: en
  Register #(.width(32)) a_23 (.D(in_23), .Q(o_23), .clk(clk), .clr(reset));  // open: en
  Register #(.width(32)) a_27 (.D(in_27), .Q(o_27), .clk(clk), .clr(reset));  // open: en
  Register #(.width(32)) a_31 (.D(in_31), .Q(o_31), .clk(clk), .clr(reset));  // open: en
  assign in_00 = demultiplexer_1_out0 & {32{1'b0}};  // AND_Gate and_1, 32 bits wide
  // Probe on A3
  Demultiplexer #(.select(5), .width(32), .tristate("true")) demultiplexer_1 (
    .out0(demultiplexer_1_out0), .out1(in_01), .out2(in_02), .out3(in_03), .out4(in_04), .out5(in_05),
    .out6(in_06), .out7(in_07), .out8(in_08), .out9(in_09), .out10(in_10), .out11(in_11), .out12(in_12),
    .out13(in_13), .out14(in_14), .out15(in_15), .out16(in_16), .out17(in_17), .out18(in_18), .out19(in_19),
    .out20(in_20), .out21(in_21), .out22(in_22), .out23(in_23), .out24(in_24), .out25(in_25), .out26(in_26),
    .out27(in_27), .out28(in_28), .out29(o_10), .out30(in_30), .out31(demultiplexer_1_out31), .in(WD),
    .sel(A3), .en(WE));
  Multiplexer #(.select(5), .width(32)) multiplexer_1 (
    .in0({32{1'b0}}), .in1(o_01), .in2(o_02), .in3(o_03), .in4(o_04), .in5(o_05), .in6(undriven_2),
    .in7(o_07), .in8(o_08), .in9(o_09), .in10(o_10), .in11(o_11), .in12(o_12), .in13(o_13), .in14(o_14),
    .in15(o_15), .in16(o_16), .in17(o_17), .in18(o_18), .in19(o_19), .in20(o_20), .in21(o_21), .in22(o_22),
    .in23(o_23), .in24(o_24), .in25(o_25), .in26(o_26), .in27(o_27), .in28(o_28), .in29(o_29), .in30(o_30),
    .in31(o_31), .out(RD1), .sel(A1));  // open: en
  Multiplexer #(.select(5), .width(32)) multiplexer_2 (
    .in0({32{1'b0}}), .in1(o_01), .in2(o_02), .in3(o_03), .in4(o_04), .in5(o_05), .in6(o_06), .in7(o_07),
    .in8(o_08), .in9(o_09), .in10(o_10), .in11(o_11), .in12(o_12), .in13(o_13), .in14(a_06), .in15(o_15),
    .in16(o_16), .in17(o_17), .in18(o_18), .in19(o_19), .in20(o_20), .in21(o_21), .in22(o_22), .in23(o_23),
    .in24(o_24), .in25(o_25), .in26(o_26), .in27(o_27), .in28(o_28), .in29(o_29), .in30(o_30), .in31(o_31),
    .out(RD2), .sel(A2));  // open: en

  // Notes on the sheet:
  //   一定要把3态打开！
endmodule

module ALU (
  input  [1:0] F,
  input  [31:0] A,
  input  [31:0] B,
  output zero,
  output [31:0] result,
  output [31:0] result_2
);

  wire [31:0] adder_1_out, multiplexer_1_out, or_1_out, undriven;

  Multiplexer #(.width(32)) multiplexer_1 (.in0(B), .in1(undriven), .out(multiplexer_1_out), .sel(F[0]));  // open: en
  assign or_1_out = B | A;  // OR_Gate or_1, 32 bits wide
  Adder #(.width(32)) adder_1 (.a(A), .b(multiplexer_1_out), .out(adder_1_out), .cin(F[0]));  // open: cout
  Multiplexer #(.width(32)) multiplexer_2 (.in0(adder_1_out), .in1(or_1_out), .out(result), .sel(F[1]));  // open: en
  Comparator #(.width(32)) comparator_1 (.a({32{1'b0}}), .b(adder_1_out), .eq(zero));  // open: gt, lt

  assign result_2 = result;

  // Other names for the same wires on the sheet: cin = F[0]; is_sub = F[0]; is_or = F[1]
endmodule

module DM (
  input  [31:0] addr,
  input  [31:0] WD,
  input  WE,
  input  clk,
  input  reset,
  output [31:0] RD
);

  wire [11:0] bitselector_1_out;
  wire [31:0] shifter_1_out;

  Shifter #(.width(32), .shift("lr")) shifter_1 (.in(addr), .\dist (5'b00010), .out(shifter_1_out));
  BitSelector #(.width(32), .group(12)) bitselector_1 (.in(shifter_1_out), .out(bitselector_1_out), .sel(2'b00));
  RAM #(.addrWidth(12), .dataWidth(32), .bus("separate")) ram_1 (
    .addr(bitselector_1_out), .din(WD), .data(RD), .str(WE), .clk(clk), .clr(reset));  // open: sel, ld
endmodule

module Controller (
  input  [5:0] funct,
  input  [5:0] op,
  output [1:0] nPC_Sel,
  output RegDst,
  output ALUSrc,
  output MemtoReg,
  output RegWrite,
  output MemWrite,
  output ExtOp,
  output [2:0] ALU_op
);

  wire add, beq, comparator_1_eq, comparator_6_eq, comparator_7_eq, lui, lw, ori, sub, sw, undriven;

  Comparator #(.width(6), .mode("unsigned")) comparator_1 (
    .a(op), .b({6{1'b0}}), .eq(comparator_1_eq));  // open: gt, lt
  Comparator #(.width(6), .mode("unsigned")) comparator_2 (.a(op), .b(6'b001101), .eq(ori));  // open: gt, lt
  Comparator #(.width(6), .mode("unsigned")) comparator_3 (.a(op), .b(6'b101011), .eq(sw));  // open: gt, lt
  Comparator #(.width(6), .mode("unsigned")) comparator_4 (.a(op), .b(6'b000100), .eq(beq));  // open: gt, lt
  Comparator #(.width(6), .mode("unsigned")) comparator_5 (.a(op), .b(6'b001111), .eq(lui));  // open: gt, lt
  Comparator #(.width(6), .mode("unsigned")) comparator_6 (
    .a(6'b100000), .b(funct), .eq(comparator_6_eq));  // open: gt, lt
  Comparator #(.width(6), .mode("unsigned")) comparator_7 (
    .a(6'b100010), .b(funct), .eq(comparator_7_eq));  // open: gt, lt
  and and_1 (add, comparator_6_eq, comparator_1_eq);
  and and_2 (sub, comparator_7_eq, comparator_1_eq);
  or or_1 (RegDst, add, sub);
  buf or_2 (ALU_op[2], 1'b0);  // OR_Gate
  or or_3 (ALUSrc, ori, lw, sw, beq);
  buf or_4 (MemtoReg, lw);  // OR_Gate
  or or_5 (ALU_op[0], sub, beq, add);
  or or_6 (RegWrite, add, sub, ori, lw, beq);
  buf or_7 (MemWrite, sw);  // OR_Gate
  or or_8 (nPC_Sel[1], 1'b0, undriven);
  buf or_9 (nPC_Sel[0], beq);  // OR_Gate
  or or_10 (ExtOp, lw, sw);

  // Notes on the sheet:
  //   delete it when need
endmodule

module ALU_2 (
  input  [31:0] A,
  input  [31:0] B,
  input  [31:0] B_2,
  input  [2:0] ALUop,
  output zero,
  output [31:0] out_6
);

  wire [31:0] adder_1_out, or_1_out, shifter_1_out, undriven;

  Adder #(.width(32)) adder_1 (.a(A), .b(B), .out(adder_1_out));  // open: cin, cout
  assign or_1_out = A | B;  // OR_Gate or_1, 32 bits wide
  Shifter #(.width(32)) shifter_1 (.in(B), .\dist (5'b10000), .out(shifter_1_out));
  Comparator #(.width(32), .mode("unsigned")) comparator_1 (.a(A), .b(B), .eq(zero));  // open: gt, lt
  Multiplexer #(.select(3), .width(32)) result (
    .in0(adder_1_out), .in1(undriven), .in2(or_1_out), .in3(shifter_1_out), .out(out_6), .sel(ALUop));  // open: in4, in5, in6, in7, en

  assign B_2 = B;

  // Notes on the sheet:
  //   lui 将低16位移动到高16位
  //   lui 将低16位移动到高16位
endmodule

module EXT (
  input  [15:0] Input,
  input  EXT_op,
  input  EXT_op_2,
  output [31:0] Out
);

  wire undriven;
  wire [31:0] bit_extender_1_out, bit_extender_2_out;

  assign bit_extender_1_out = {{16{1'b0}}, Input};  // Bit_Extender bit_extender_1
  assign bit_extender_2_out = {{16{Input[15]}}, Input};  // Bit_Extender bit_extender_2
  assign bit_extender_2_out = {{16{Input[15]}}, Input};  // Bit_Extender bit_extender_3
  Multiplexer #(.width(32)) multiplexer_1 (
    .in0(bit_extender_1_out), .in1(bit_extender_2_out), .out(Out), .sel(EXT_op), .en(undriven));
  Multiplexer #(.width(32)) multiplexer_2 (
    .in0(bit_extender_1_out), .in1(bit_extender_2_out), .out(Out), .sel(EXT_op), .en(undriven));

  assign EXT_op_2 = EXT_op;
endmodule
