// Logisim project 2^n_mod5-mealy.circ as structural Verilog: 1 circuit, main circuit mod5
module mod5 (
  input  b,
  output out_2,
  output out_3,
  output out_4,
  output out_5,
  output out_6
);

  wire and_1_out, and_2_out, and_3_out, and_4_out, clock_1_out, counter_1_q, multiplexer_1_out, not_1_out,
       not_2_out, not_3_out, not_4_out, or_1_out, or_2_out, or_3_out, or_4_out, q0_q, q1_q, q2_q, q3_q;

  not not_1 (not_1_out, b);
  or or_1 (or_1_out, multiplexer_1_out, q2_q);
  not not_2 (not_2_out, b);
  or or_2 (or_2_out, q1_q, q3_q);
  and and_1 (and_1_out, not_1_out, or_1_out);
  and and_2 (and_2_out, or_1_out, b);
  and and_3 (and_3_out, not_2_out, or_2_out);
  and and_4 (and_4_out, or_2_out, b);
  Clock clock_1 (.out(clock_1_out));
  D_Flip_Flop q0 (.clk(clock_1_out), .D(and_1_out), .Q(q0_q));  // open: Qn, preset, en, reset
  D_Flip_Flop q1 (.clk(clock_1_out), .D(and_2_out), .Q(q1_q));  // open: Qn, preset, en, reset
  D_Flip_Flop q2 (.clk(clock_1_out), .D(and_3_out), .Q(q2_q));  // open: Qn, preset, en, reset
  D_Flip_Flop q3 (.clk(clock_1_out), .D(and_4_out), .Q(q3_q));  // open: Qn, preset, en, reset
  Counter #(.width(1), .max('h1), .ongoal("stay")) counter_1 (
    .Q(counter_1_q), .clk(clock_1_out));  // open: load, D, count, carry, clr
  Multiplexer multiplexer_1 (.in0(1'b1), .in1(q0_q), .out(multiplexer_1_out), .sel(counter_1_q));  // open: en
  or or_3 (or_3_out, multiplexer_1_out, q2_q);
  or or_4 (or_4_out, q1_q, q3_q);
  not not_3 (not_3_out, b);
  not not_4 (not_4_out, b);
  and and_5 (out_3, not_4_out, or_3_out);
  and and_6 (out_4, b, or_3_out);
  and and_7 (out_5, b, or_4_out);
  and and_8 (out_6, not_3_out, or_4_out);

  assign out_2 = 1'b0;

  // Notes on the sheet:
  //   小心不小心并联的地方哦！！
endmodule
