// Logisim project pre_sokoban.circ as structural Verilog: 2 circuits, main circuit Sokoban
module Sokoban (
  input  dx,
  input  dy,
  input  clk,
  input  reset,
  output \output ,
  output flag
);

  wire comparator_1_eq, comparator_2_eq, is_valid, not_1_out, not_2_out, not_3_out, register_3_q;
  wire [2:0] bit_extender_1_out, bit_extender_2_out, multiplexer_1_out, multiplexer_2_out, new_x, new_y, x, y;

  assign bit_extender_1_out = {{2{1'b0}}, dx};  // Bit_Extender bit_extender_1
  // Probe on x
  assign bit_extender_2_out = {{2{1'b0}}, dy};  // Bit_Extender bit_extender_2
  // Probe on y
  // Probe on new_x
  Adder #(.width(3)) adder_1 (.a(bit_extender_1_out), .b(x), .out(new_x));  // open: cin, cout
  // Probe on new_y
  Adder #(.width(3)) adder_2 (.a(bit_extender_2_out), .b(y), .out(new_y));  // open: cin, cout
  is_valid is_valid_1 (.x(new_x), .y(new_y), .out_3(is_valid));
  Multiplexer #(.width(3)) multiplexer_1 (.in0(x), .in1(new_x), .out(multiplexer_1_out), .sel(is_valid));  // open: en
  Multiplexer #(.width(3)) multiplexer_2 (.in0(y), .in1(new_y), .out(multiplexer_2_out), .sel(is_valid));  // open: en
  // Probe on is_valid
  // Probe on multiplexer_1_out
  Register #(.width(3)) register_1 (.D(multiplexer_1_out), .Q(x), .clk(clk), .clr(reset));  // open: en
  Register #(.width(3)) register_2 (.D(multiplexer_2_out), .Q(y), .clk(clk), .clr(reset));  // open: en
  Comparator #(.width(3)) comparator_1 (.a(x), .b(3'b101), .eq(comparator_1_eq));  // open: gt, lt
  Comparator #(.width(3)) comparator_2 (.a(y), .b(3'b101), .eq(comparator_2_eq));  // open: gt, lt
  not not_1 (not_1_out, is_valid);
  and and_1 (\output , comparator_1_eq, comparator_2_eq, not_2_out);
  not not_2 (not_2_out, reset);
  Register #(.width(1)) register_3 (.D(not_1_out), .Q(register_3_q), .clk(clk), .clr(reset));  // open: en
  not not_3 (not_3_out, reset);
  and and_2 (flag, register_3_q, not_3_out);
endmodule

module is_valid (
  input  [2:0] x,
  input  [2:0] y,
  output out_3
);

  wire and_2_out, comparator_1_eq, comparator_2_eq, comparator_3_eq, comparator_4_eq, comparator_5_eq,
       comparator_6_eq, comparator_7_eq, comparator_8_eq, comparator_9_eq, comparator_10_eq,
       comparator_11_eq, comparator_12_eq, comparator_13_lt, comparator_14_lt, nand_1_out, nand_2_out,
       nand_3_out, nand_4_out, nand_5_out, nand_6_out;

  Comparator #(.width(3)) comparator_1 (.a(x), .b(3'b001), .eq(comparator_1_eq));  // open: gt, lt
  Comparator #(.width(3)) comparator_2 (.a(y), .b(3'b001), .eq(comparator_2_eq));  // open: gt, lt
  nand nand_1 (nand_1_out, comparator_2_eq, comparator_1_eq);
  Comparator #(.width(3)) comparator_3 (.a(x), .b(3'b001), .eq(comparator_3_eq));  // open: gt, lt
  Comparator #(.width(3)) comparator_4 (.a(y), .b(3'b010), .eq(comparator_4_eq));  // open: gt, lt
  nand nand_2 (nand_2_out, comparator_4_eq, comparator_3_eq);
  Comparator #(.width(3)) comparator_5 (.a(x), .b(3'b010), .eq(comparator_5_eq));  // open: gt, lt
  Comparator #(.width(3)) comparator_6 (.a(y), .b(3'b001), .eq(comparator_6_eq));  // open: gt, lt
  nand nand_3 (nand_3_out, comparator_6_eq, comparator_5_eq);
  Comparator #(.width(3)) comparator_7 (.a(x), .b(3'b011), .eq(comparator_7_eq));  // open: gt, lt
  Comparator #(.width(3)) comparator_8 (.a(y), .b(3'b100), .eq(comparator_8_eq));  // open: gt, lt
  nand nand_4 (nand_4_out, comparator_8_eq, comparator_7_eq);
  and and_1 (out_3, nand_1_out, nand_2_out, nand_3_out, nand_4_out, nand_5_out, nand_6_out, and_2_out);
  Comparator #(.width(3)) comparator_9 (.a(x), .b(3'b100), .eq(comparator_9_eq));  // open: gt, lt
  Comparator #(.width(3)) comparator_10 (.a(y), .b(3'b011), .eq(comparator_10_eq));  // open: gt, lt
  nand nand_5 (nand_5_out, comparator_10_eq, comparator_9_eq);
  Comparator #(.width(3)) comparator_11 (.a(x), .b(3'b100), .eq(comparator_11_eq));  // open: gt, lt
  Comparator #(.width(3)) comparator_12 (.a(y), .b(3'b100), .eq(comparator_12_eq));  // open: gt, lt
  nand nand_6 (nand_6_out, comparator_12_eq, comparator_11_eq);
  Comparator #(.width(3), .mode("unsigned")) comparator_13 (.a(x), .b(3'b110), .lt(comparator_13_lt));  // open: gt, eq
  Comparator #(.width(3), .mode("unsigned")) comparator_14 (.a(y), .b(3'b110), .lt(comparator_14_lt));  // open: gt, eq
  and and_2 (and_2_out, comparator_14_lt, comparator_13_lt);
endmodule
